# Fritzing sketch demo (saved by Fritzing 1.0.6)
breadboards: 1

parts:
  KY-1 = Keyes Relay [package=THT]
  Part2 = Lilypad Battery Connect
  A1 = Esp32-c3 super mini
  SW1 = Slide_Switch_new
  A2 = am312 pir sensor [package=THT]
  Componente1 = BH1750
  DS1 = DS18B20 1-Wire Temperature Sensor [part_number=DS18B20]
  OLED_I2C1 = OLED 128x64 I2C Monochrome Display
  R1 = Resistor [tolerance=±5% resistance=10k package="0603 [SMD]"]
  R2 = Resistor [tolerance=±5% resistance=4.7k package="2512 [SMD]"]
  LED1 = LEDs [package=led10mm]

nets:
  N1: KY-1.signal, A1.Pin_13
  VDD: KY-1.power, A1.Pin_16, A2.pin1, Componente1.VCC, DS1.VDD, OLED_I2C1.VDD, R2.Pin_1
  GND: KY-1.ground, A1.Pin_15, SW1.pin_1, A2.pin3, Componente1.GND, DS1.GND, OLED_I2C1.GND, R1.Pin_1
  N2: KY-1.C, Part2.+
  N3: KY-1.NO, LED1.C
  N4: Part2.-, LED1.A
  N5: A1.Pin_4, Componente1.SDA, OLED_I2C1.SDA
  N6: A1.Pin_5, Componente1.SCL, OLED_I2C1.SCK
  N7: A1.Pin_6, DS1.DQ, R2.Pin_0
  N8: A1.Pin_11, A2.pin2, R1.Pin_0
  N9: A1.Pin_12, SW1.pin_2

notes:
  220-240 V
  Switch
  5V Relay
  AM312
  SSD1306
  DS18B20
  BH1750
  10KΩ
  4.7KΩ

custom parts:
  Keyes Relay: The Keyes 5V relay module is suitable for SCM development, home appliance control. It uses a 5V~12V TIL control signal which can control DC / AC signal.
  Esp32-c3 super mini: ESP32-C3 Development Board ESP32 SuperMini Development Board ESP32 Development Board WiFi Bluetooth.
  Slide_Switch_new: the New two pin slide switch
  am312 pir sensor: The AM312 is an ultra-miniature PIR module which uses a pyroelectric sensor similar to the one found in the common SR501 but in a more compact form factor.
  BH1750: Light Sensor
  LEDs: LEDs Standard schematic elements and footprints for 5mm, 3mm, 1206, and 0603 sized LEDs. 5mm - Spark Fun Electronics SKU : COM-00529 (and others)
